// Logisim project ourcircuit.circ as structural Verilog: 25 circuits, main circuit main
module main (
);

  wire ALU_zero, button_1_out, clock_1_out, Decoder_halt, Decoder_immtoalu, Decoder_immtopc, Decoder_led,
       Decoder_memread, Decoder_memtoreg, Decoder_memwrite, Decoder_pctoreg, Decoder_regtopc,
       Decoder_regwrite, Decoder_shiftertoreg, Decoder_shiftsrc, Decoder_writeled, Decoder_zerostoalu,
       EX_MEM_led_2, EX_MEM_memread_2, EX_MEM_memtoreg_2, EX_MEM_memwrite_2, EX_MEM_pctoreg_2,
       EX_MEM_regwrite_2, EX_MEM_shiftertoreg_2, EX_MEM_shiftsrc_2, EX_MEM_subop_2, EX_MEM_writeled_2,
       forwarding_unit_1_a_ex_mem, forwarding_unit_1_a_mem_wb, forwarding_unit_1_b_ex_mem,
       forwarding_unit_1_b_mem_wb, ID_EX_immtoalu_2, ID_EX_led_2, ID_EX_memread_2, ID_EX_memtoreg_2,
       ID_EX_memwrite_2, ID_EX_pctoreg_2, ID_EX_regwrite_2, ID_EX_shiftertoreg_2, ID_EX_shiftsrc_2,
       ID_EX_subop_2, ID_EX_writeled_2, ID_EX_zerostoalu_2, IF_ID_halt_out, Instruction_Splitter_subop,
       Instruction_Splitter_unsigned, MEM_WB_led_2, MEM_WB_memtoreg_2, MEM_WB_pctoreg_2, MEM_WB_regwrite_2,
       MEM_WB_shiftertoreg_2, MEM_WB_shiftsrc_2, MEM_WB_subop_2, MEM_WB_writeled_2, not_1_out,
       ResultToLess_less;
  wire [2:0] EX_MEM_writeregister_2, ID_EX_rtreg_2, ID_EX_writeregister_2,
       Instruction_Splitter_readregister1, Instruction_Splitter_readregister2,
       Instruction_Splitter_writeregister, MEM_WB_writeregister_2;
  wire [3:0] Decoder_aluop, EX_MEM_shiftamount_2, ID_EX_aluop_2, ID_EX_shiftamount_2,
       Instruction_Splitter_opcode, Instruction_Splitter_shiftamount, MEM_WB_shiftamount_2;
  wire [7:0] adder_1_out, EX_MEM_pc_1_2, ID_EX_pc_1_2, Instruction_Splitter_immediate, MEM_WB_pc_1_2,
       multiplexer_1_out, multiplexer_3_out, PC_q, RegistertoAddress_2_address, RegistertoAddress_address;
  wire [15:0] ALU_result, bit_extender_1_out, EX_MEM_alu_result_2, EX_MEM_readdata1_2, EX_MEM_readdata2_2,
       ID_EX_readdata1_2, ID_EX_readdata2_2,
       ID_EX_the_signal_that_goes_into_the_mux_that_goes_into_the_alu_2, IF_ID_rom_out, MEM_WB_alu_result_2,
       MEM_WB_ram_data_2, MEM_WB_readdata1_2, MEM_WB_readdata2_2, multiplexer_2_out, multiplexer_4_out,
       multiplexer_5_out, multiplexer_6_out, multiplexer_7_out, multiplexer_8_out, multiplexer_9_out,
       multiplexer_10_out, multiplexer_11_out, multiplexer_12_out, ram_1_data, register_1_q,
       Registers_readdata1, Registers_readdata2, rom_1_data, Shifter_shiftout, Sign_Extend_signextendedimm;

  Register PC (.D(multiplexer_3_out), .en(not_1_out), .Q(PC_q), .clk(clock_1_out), .clr(button_1_out));
  not not_1 (not_1_out, IF_ID_halt_out);
  Button button_1 (.out(button_1_out));
  Clock clock_1 (.out(clock_1_out));
  Adder adder_1 (.a(PC_q), .b(8'h1), .out(adder_1_out));  // open: cin, cout
  IF_ID IF_ID (
    .ROM_in(rom_1_data), .Halt_in(Decoder_halt), .clk(clock_1_out), .ROM_out(IF_ID_rom_out),
    .Halt_out(IF_ID_halt_out));
  ROM #(.dataWidth(16)) rom_1 (.addr(PC_q), .data(rom_1_data), .sel(1'b1));
  InstructionSplitter Instruction_Splitter (
    .Instruction(IF_ID_rom_out), .Opcode(Instruction_Splitter_opcode),
    .ReadRegister1(Instruction_Splitter_readregister1), .ReadRegister2(Instruction_Splitter_readregister2),
    .WriteRegister(Instruction_Splitter_writeregister), .ShiftAmount(Instruction_Splitter_shiftamount),
    .SubOp(Instruction_Splitter_subop), .Unsigned(Instruction_Splitter_unsigned),
    .Immediate(Instruction_Splitter_immediate));
  SignExtend Sign_Extend (
    .Unsigned(Instruction_Splitter_unsigned), .Immediate(Instruction_Splitter_immediate),
    .SignExtendedImm(Sign_Extend_signextendedimm));
  Decoder Decoder (
    .Opcode(Instruction_Splitter_opcode), .Subop(Instruction_Splitter_subop), .Zero(ALU_zero),
    .Less(ResultToLess_less), .ShiftSrc(Decoder_shiftsrc), .ShifterToReg(Decoder_shiftertoreg),
    .RegWrite(Decoder_regwrite), .ALUOp(Decoder_aluop), .IMMtoALU(Decoder_immtoalu),
    .RegtoPC(Decoder_regtopc), .IMMtoPC(Decoder_immtopc), .ZerosToALU(Decoder_zerostoalu),
    .MemWrite(Decoder_memwrite), .MemtoReg(Decoder_memtoreg), .Halt(Decoder_halt), .LED(Decoder_led),
    .WriteLED(Decoder_writeled), .MemRead(Decoder_memread), .PCtoReg(Decoder_pctoreg));
  ResultToLess ResultToLess (.Result(ALU_result), .Less(ResultToLess_less));
  RegisterFile Registers (
    .ReadRegister1(Instruction_Splitter_readregister1), .ReadRegister2(Instruction_Splitter_readregister2),
    .WriteRegister(MEM_WB_writeregister_2), .WriteData(multiplexer_12_out), .WriteEnable(MEM_WB_regwrite_2),
    .Clock(clock_1_out), .ReadData1(Registers_readdata1), .ReadData2(Registers_readdata2));
  Multiplexer #(.width(8), .disabled(0), .enable("false")) multiplexer_1 (
    .in0(adder_1_out), .in1(Instruction_Splitter_immediate), .out(multiplexer_1_out), .sel(Decoder_immtopc));
  Multiplexer #(.width(16), .disabled(0), .enable("false")) multiplexer_2 (
    .in0(Registers_readdata2), .in1(Sign_Extend_signextendedimm), .out(multiplexer_2_out),
    .sel(Decoder_immtoalu));
  ALUtoPC RegistertoAddress (.ALUOut(Registers_readdata1), .Address(RegistertoAddress_address));
  Multiplexer #(.width(8), .disabled(0), .enable("false")) multiplexer_3 (
    .in0(multiplexer_1_out), .in1(RegistertoAddress_address), .out(multiplexer_3_out), .sel(Decoder_regtopc));
  Multiplexer #(.width(16), .enable("false")) multiplexer_4 (
    .in0(multiplexer_9_out), .in1(ID_EX_the_signal_that_goes_into_the_mux_that_goes_into_the_alu_2),
    .out(multiplexer_4_out), .sel(ID_EX_immtoalu_2));
  Multiplexer #(.width(16), .disabled(0), .enable("false")) multiplexer_5 (
    .in0(multiplexer_4_out), .in1({16{1'b0}}), .out(multiplexer_5_out), .sel(ID_EX_zerostoalu_2));
  ID_EX ID_EX (
    .ReadData1(Registers_readdata1),
    .The_signal_that_goes_into_the_mux_that_goes_into_the_ALU(multiplexer_2_out),
    .ReadData2(Registers_readdata2), .SubOp(Instruction_Splitter_subop), .ShiftSrc(Decoder_shiftsrc),
    .ShiftAmount(Instruction_Splitter_shiftamount), .PC_1(adder_1_out), .ZerosToALU(Decoder_zerostoalu),
    .MemWrite(Decoder_memwrite), .MemToReg(Decoder_memtoreg), .LED(Decoder_led), .WriteLED(Decoder_writeled),
    .MemRead(Decoder_memread), .PCtoReg(Decoder_pctoreg), .ShifterToReg(Decoder_shiftertoreg),
    .ALUOp(Decoder_aluop), .RegWrite(Decoder_regwrite), .WriteRegister(Instruction_Splitter_writeregister),
    .rtReg(Instruction_Splitter_readregister2), .IMMtoALU(Decoder_immtoalu), .clk(clock_1_out),
    .ReadData1_2(ID_EX_readdata1_2),
    .The_signal_that_goes_into_the_mux_that_goes_into_the_ALU_2(ID_EX_the_signal_that_goes_into_the_mux_that_goes_into_the_alu_2),
    .ReadData2_2(ID_EX_readdata2_2), .SubOp_2(ID_EX_subop_2), .ShiftSrc_2(ID_EX_shiftsrc_2),
    .ShiftAmount_2(ID_EX_shiftamount_2), .PC_1_2(ID_EX_pc_1_2), .ZerosToALU_2(ID_EX_zerostoalu_2),
    .MemWrite_2(ID_EX_memwrite_2), .MemToReg_2(ID_EX_memtoreg_2), .LED_2(ID_EX_led_2),
    .WriteLED_2(ID_EX_writeled_2), .MemRead_2(ID_EX_memread_2), .PCtoReg_2(ID_EX_pctoreg_2),
    .ShifterToReg_2(ID_EX_shiftertoreg_2), .ALUOp_2(ID_EX_aluop_2), .RegWrite_2(ID_EX_regwrite_2),
    .WriteRegister_2(ID_EX_writeregister_2), .rtReg_2(ID_EX_rtreg_2), .IMMtoALU_2(ID_EX_immtoalu_2));
  sixteen_bit_ALU ALU (
    .ALUOperation(ID_EX_aluop_2), .a(multiplexer_8_out), .b(multiplexer_5_out), .Zero(ALU_zero),
    .Result(ALU_result));  // open: Overflow
  Multiplexer #(.width(16), .enable("false")) multiplexer_6 (
    .in0(ID_EX_readdata1_2), .in1(multiplexer_12_out), .out(multiplexer_6_out),
    .sel(forwarding_unit_1_a_mem_wb));
  Multiplexer #(.width(16), .enable("false")) multiplexer_7 (
    .in0(ID_EX_readdata2_2), .in1(multiplexer_12_out), .out(multiplexer_7_out),
    .sel(forwarding_unit_1_b_mem_wb));
  Forwarding_Unit forwarding_unit_1 (
    .rs_ID_EX(ID_EX_writeregister_2), .rt_ID_EX(ID_EX_rtreg_2), .WriteReg_MEM_WB(MEM_WB_writeregister_2),
    .WriteReg_EM_MEM(EX_MEM_writeregister_2), .RegWrite_EX_MEM(ID_EX_regwrite_2),
    .RegWrite_MEM_WB(MEM_WB_regwrite_2), .A_EX_MEM(forwarding_unit_1_a_ex_mem),
    .A_MEM_WB(forwarding_unit_1_a_mem_wb), .B_EX_MEM(forwarding_unit_1_b_ex_mem),
    .B_MEM_WB(forwarding_unit_1_b_mem_wb));
  Multiplexer #(.width(16), .enable("false")) multiplexer_8 (
    .in0(multiplexer_6_out), .in1(EX_MEM_alu_result_2), .out(multiplexer_8_out),
    .sel(forwarding_unit_1_a_ex_mem));
  Multiplexer #(.width(16), .enable("false")) multiplexer_9 (
    .in0(multiplexer_7_out), .in1(EX_MEM_alu_result_2), .out(multiplexer_9_out),
    .sel(forwarding_unit_1_b_ex_mem));
  ALUtoPC RegistertoAddress_2 (.ALUOut(EX_MEM_readdata2_2), .Address(RegistertoAddress_2_address));
  EX_MEM EX_MEM (
    .ReadData1(multiplexer_8_out), .ALU_Result(ALU_result), .ReadData2(ID_EX_readdata2_2),
    .SubOp(ID_EX_subop_2), .ShiftSrc(ID_EX_shiftsrc_2), .ShiftAmount(ID_EX_shiftamount_2),
    .PC_1(ID_EX_pc_1_2), .ShifterToReg(ID_EX_shiftertoreg_2), .MemWrite(ID_EX_memwrite_2),
    .MemToReg(ID_EX_memtoreg_2), .LED(ID_EX_led_2), .WriteLED(ID_EX_writeled_2), .MemRead(ID_EX_memread_2),
    .PCtoReg(ID_EX_pctoreg_2), .RegWrite(ID_EX_regwrite_2), .WriteRegister(ID_EX_writeregister_2),
    .clk(clock_1_out), .ReadData1_2(EX_MEM_readdata1_2), .ALU_Result_2(EX_MEM_alu_result_2),
    .ReadData2_2(EX_MEM_readdata2_2), .SubOp_2(EX_MEM_subop_2), .ShiftSrc_2(EX_MEM_shiftsrc_2),
    .ShiftAmount_2(EX_MEM_shiftamount_2), .PC_1_2(EX_MEM_pc_1_2), .ShifterToReg_2(EX_MEM_shiftertoreg_2),
    .MemWrite_2(EX_MEM_memwrite_2), .MemToReg_2(EX_MEM_memtoreg_2), .LED_2(EX_MEM_led_2),
    .WriteLED_2(EX_MEM_writeled_2), .MemRead_2(EX_MEM_memread_2), .PCtoReg_2(EX_MEM_pctoreg_2),
    .RegWrite_2(EX_MEM_regwrite_2), .WriteRegister_2(EX_MEM_writeregister_2));
  RAM #(.dataWidth(16), .bus("separate")) ram_1 (
    .addr(RegistertoAddress_2_address), .din(EX_MEM_readdata1_2), .data(ram_1_data), .str(EX_MEM_memwrite_2),
    .sel(1'b1), .clk(clock_1_out), .ld(EX_MEM_memread_2));  // open: clr
  MEM_WB MEM_WB (
    .RAM_Data(ram_1_data), .ALU_Result(EX_MEM_alu_result_2), .SubOp(EX_MEM_subop_2),
    .ReadData1(EX_MEM_readdata1_2), .ReadData2(EX_MEM_readdata2_2), .ShiftSrc(EX_MEM_shiftsrc_2),
    .ShiftAmount(EX_MEM_shiftamount_2), .PC_1(EX_MEM_pc_1_2), .ShifterToReg(EX_MEM_shiftertoreg_2),
    .PCtoReg(EX_MEM_pctoreg_2), .MemToReg(EX_MEM_memtoreg_2), .LED(EX_MEM_led_2),
    .WriteLED(EX_MEM_writeled_2), .RegWrite(EX_MEM_regwrite_2), .WriteRegister(EX_MEM_writeregister_2),
    .clk(clock_1_out), .RAM_Data_2(MEM_WB_ram_data_2), .ALU_Result_2(MEM_WB_alu_result_2),
    .SubOp_2(MEM_WB_subop_2), .ReadData1_2(MEM_WB_readdata1_2), .ReadData2_2(MEM_WB_readdata2_2),
    .ShiftSrc_2(MEM_WB_shiftsrc_2), .ShiftAmount_2(MEM_WB_shiftamount_2), .PC_1_2(MEM_WB_pc_1_2),
    .ShifterToReg_2(MEM_WB_shiftertoreg_2), .PCtoReg_2(MEM_WB_pctoreg_2), .MemToReg_2(MEM_WB_memtoreg_2),
    .LED_2(MEM_WB_led_2), .WriteLED_2(MEM_WB_writeled_2), .RegWrite_2(MEM_WB_regwrite_2),
    .WriteRegister_2(MEM_WB_writeregister_2));
  Multiplexer #(.width(16), .disabled(0), .enable("false")) multiplexer_10 (
    .in0(MEM_WB_alu_result_2), .in1(MEM_WB_ram_data_2), .out(multiplexer_10_out), .sel(MEM_WB_memtoreg_2));
  Shifter Shifter (
    .Subop(MEM_WB_subop_2), .Data(MEM_WB_readdata1_2), .ShamtReg(MEM_WB_readdata2_2),
    .ShiftSrc(MEM_WB_shiftsrc_2), .Shamt(MEM_WB_shiftamount_2), .ShiftOut(Shifter_shiftout));
  Multiplexer #(.width(16), .disabled(0), .enable("false")) multiplexer_11 (
    .in0(multiplexer_10_out), .in1(Shifter_shiftout), .out(multiplexer_11_out), .sel(MEM_WB_shiftertoreg_2));
  assign bit_extender_1_out = {{8{1'b0}}, MEM_WB_pc_1_2};  // Bit_Extender bit_extender_1
  Multiplexer #(.width(16), .disabled(0), .enable("false")) multiplexer_12 (
    .in0(multiplexer_11_out), .in1(bit_extender_1_out), .out(multiplexer_12_out), .sel(MEM_WB_pctoreg_2));
  Hex_Digit_Display hex_digit_display_1 (.value(register_1_q[11:8]));  // open: dp
  Hex_Digit_Display hex_digit_display_2 (.value(register_1_q[15:12]));  // open: dp
  Register #(.width(16)) register_1 (
    .D(MEM_WB_readdata1_2), .en(MEM_WB_writeled_2), .Q(register_1_q), .clk(clock_1_out));  // open: clr
  LED Halt (.in(MEM_WB_led_2));
  Hex_Digit_Display hex_digit_display_3 (.value(register_1_q[7:4]));  // open: dp
  Hex_Digit_Display hex_digit_display_4 (.value(register_1_q[3:0]));  // open: dp

  // Notes on the sheet:
  //   contents of rom_1 (hex, n*v repeats v):
  //   1 1104 241 1303 40 f000 241 1300 481 1503 281 6c1 1705 2c1 f200 901 1900 18ff f800 b41 1bf0 1b0f
  //   fa00 d81 1d19 fc1 1f20 3dc0 fc00 1 11e0 241 1378 3041 f000 481 150d 6c1 1708 44c0 f400 901 1910 b41
  //   1b04 4941 f800 d81 1d02 5c02 fc00 fc1 1f10 5e03 fe00 1 1140 61c1 63c0 f200 481 15ff 6c1 1701 845b
  //   865b 901 1900 985f b41 1b00 d81 1d00 1ce9 aa63 ac63 fc1 1f00 1 1119 be67 b067 e054 7000 c259 6c1
  //   170a f600 7000 d200 7000 fc1 1f01 fe00 7000 fc1 1f02 fe00 7000 fc1 1f03 fe00 7000 fc1 1f04 fe00 7000
endmodule

module InstructionSplitter (
  input  [15:0] Instruction,
  output [3:0] Opcode,
  output [2:0] ReadRegister1,
  output [2:0] ReadRegister2,
  output [2:0] WriteRegister,
  output [3:0] ShiftAmount,
  output SubOp,
  output Unsigned,
  output [7:0] Immediate
);


  assign Immediate = Instruction[7:0];
  assign Opcode = Instruction[15:12];
  assign ReadRegister1 = Instruction[11:9];
  assign ReadRegister2 = Instruction[8:6];
  assign ShiftAmount = Instruction[4:1];
  assign SubOp = Instruction[0];
  assign Unsigned = Instruction[8];
  assign WriteRegister = Instruction[11:9];
endmodule

module SignExtend (
  input  Unsigned,
  input  [7:0] Immediate,
  output [15:0] SignExtendedImm
);

  wire [15:0] bit_extender_1_out, bit_extender_2_out;

  assign bit_extender_1_out = {{8{Immediate[7]}}, Immediate};  // Bit_Extender bit_extender_1
  assign bit_extender_2_out = {{8{1'b0}}, Immediate};  // Bit_Extender bit_extender_2
  Multiplexer #(.width(16), .disabled(0), .enable("false")) multiplexer_1 (
    .in0(bit_extender_1_out), .in1(bit_extender_2_out), .out(SignExtendedImm), .sel(Unsigned));
endmodule

module ALUtoPC (
  input  [15:0] ALUOut,
  output [7:0] Address
);


  assign Address = ALUOut[7:0];
endmodule

module Shifter (
  input  Subop,
  input  [15:0] Data,
  input  [15:0] ShamtReg,
  input  ShiftSrc,
  input  [3:0] Shamt,
  output [15:0] ShiftOut
);

  wire [3:0] multiplexer_1_out;
  wire [15:0] shifter_1_out, shifter_2_out;

  Multiplexer #(.width(4), .disabled(0), .enable("false")) multiplexer_1 (
    .in0(ShamtReg[3:0]), .in1(Shamt), .out(multiplexer_1_out), .sel(ShiftSrc));
  Shifter_part #(.width(16)) shifter_1 (.in(Data), .\dist (multiplexer_1_out), .out(shifter_1_out));
  Shifter_part #(.width(16), .shift("lr")) shifter_2 (.in(Data), .\dist (multiplexer_1_out), .out(shifter_2_out));
  Multiplexer #(.width(16), .disabled(0), .enable("false")) multiplexer_2 (
    .in0(shifter_1_out), .in1(shifter_2_out), .out(ShiftOut), .sel(Subop));
endmodule

module RegisterFile (
  input  [2:0] ReadRegister1,
  input  [2:0] ReadRegister2,
  input  [2:0] WriteRegister,
  input  [15:0] WriteData,
  input  WriteEnable,
  input  Clock,
  output [15:0] ReadData1,
  output [15:0] ReadData2
);

  wire decoder_1_out0, decoder_1_out1, decoder_1_out2, decoder_1_out3, decoder_1_out4, decoder_1_out5,
       decoder_1_out6, decoder_1_out7;
  wire [15:0] register_1_q, register_2_q, register_3_q, register_4_q, register_5_q, register_6_q,
       register_7_q, register_8_q;

  Decoder_part #(.select(3), .disabled(0)) decoder_1 (
    .out0(decoder_1_out0), .out1(decoder_1_out1), .out2(decoder_1_out2), .out3(decoder_1_out3),
    .out4(decoder_1_out4), .out5(decoder_1_out5), .out6(decoder_1_out6), .out7(decoder_1_out7),
    .sel(WriteRegister), .en(WriteEnable));
  Register #(.width(16), .trigger("falling")) register_1 (
    .D(WriteData), .en(decoder_1_out0), .Q(register_1_q), .clk(Clock));  // open: clr
  Register #(.width(16), .trigger("falling")) register_2 (
    .D(WriteData), .en(decoder_1_out1), .Q(register_2_q), .clk(Clock));  // open: clr
  Register #(.width(16), .trigger("falling")) register_3 (
    .D(WriteData), .en(decoder_1_out2), .Q(register_3_q), .clk(Clock));  // open: clr
  Register #(.width(16), .trigger("falling")) register_4 (
    .D(WriteData), .en(decoder_1_out3), .Q(register_4_q), .clk(Clock));  // open: clr
  Register #(.width(16), .trigger("falling")) register_5 (
    .D(WriteData), .en(decoder_1_out4), .Q(register_5_q), .clk(Clock));  // open: clr
  Register #(.width(16), .trigger("falling")) register_6 (
    .D(WriteData), .en(decoder_1_out5), .Q(register_6_q), .clk(Clock));  // open: clr
  Register #(.width(16), .trigger("falling")) register_7 (
    .D(WriteData), .en(decoder_1_out6), .Q(register_7_q), .clk(Clock));  // open: clr
  Register #(.width(16), .trigger("falling")) register_8 (
    .D(WriteData), .en(decoder_1_out7), .Q(register_8_q), .clk(Clock));  // open: clr
  Multiplexer #(.select(3), .width(16), .enable("false")) multiplexer_1 (
    .in0(register_1_q), .in1(register_2_q), .in2(register_3_q), .in3(register_4_q), .in4(register_5_q),
    .in5(register_6_q), .in6(register_7_q), .in7(register_8_q), .out(ReadData1), .sel(ReadRegister1));
  Multiplexer #(.select(3), .width(16), .enable("false")) multiplexer_2 (
    .in0(register_1_q), .in1(register_2_q), .in2(register_3_q), .in3(register_4_q), .in4(register_5_q),
    .in5(register_6_q), .in6(register_7_q), .in7(register_8_q), .out(ReadData2), .sel(ReadRegister2));
endmodule

module ShifterDecoder (
  input  [3:0] Opcode,
  output ShiftSrc,
  output ShiftertoReg,
  output RegWrite
);

  and and_1 (RegWrite, ~Opcode[3], Opcode[2], ~Opcode[1]);  // AND_Gate

  assign ShiftertoReg = RegWrite;
  assign ShiftSrc = Opcode[0];
endmodule

module Arith_Log_Decoder (
  input  [3:0] Opcode,
  input  Subop,
  output [3:0] ALUOperation,
  output RegWrite,
  output ALUSrc
);

  wire and_1_out, and_3_out, and_4_out, and_5_out, and_6_out, and_7_out, not_1_out, not_2_out, not_3_out,
       not_4_out, not_5_out, not_6_out, not_7_out, not_8_out, not_9_out, not_10_out, not_11_out, not_12_out,
       not_13_out, not_14_out, not_15_out, not_16_out, not_17_out, not_18_out, not_19_out, not_20_out,
       not_21_out;

  and and_1 (and_1_out, ~Opcode[3], ~Opcode[2], Opcode[1], ~Opcode[0]);  // AND_Gate
  not not_1 (not_1_out, Opcode[3]);
  not not_2 (not_2_out, Opcode[2]);
  not not_3 (not_3_out, Subop);
  not not_4 (not_4_out, Opcode[3]);
  not not_5 (not_5_out, Opcode[2]);
  not not_6 (not_6_out, Opcode[1]);
  not not_7 (not_7_out, Opcode[0]);
  not not_8 (not_8_out, Opcode[3]);
  not not_9 (not_9_out, Opcode[2]);
  not not_10 (not_10_out, Subop);
  not not_11 (not_11_out, Opcode[3]);
  not not_12 (not_12_out, Opcode[2]);
  not not_13 (not_13_out, Opcode[1]);
  not not_14 (not_14_out, Opcode[3]);
  not not_15 (not_15_out, Opcode[2]);
  not not_16 (not_16_out, Opcode[1]);
  not not_17 (not_17_out, Opcode[3]);
  not not_18 (not_18_out, Opcode[2]);
  not not_19 (not_19_out, Opcode[3]);
  not not_20 (not_20_out, Opcode[2]);
  not not_21 (not_21_out, Opcode[1]);
  and and_2 (ALUOperation[3], not_1_out, not_2_out, Opcode[1], Opcode[0], not_3_out);
  and and_3 (and_3_out, not_4_out, not_5_out, not_6_out, not_7_out, Subop);
  and and_4 (and_4_out, not_8_out, not_9_out, Opcode[1], Opcode[0], not_10_out);
  and and_5 (and_5_out, not_11_out, not_12_out, not_13_out);
  and and_6 (and_6_out, not_14_out, not_15_out, not_16_out);
  and and_7 (and_7_out, not_17_out, not_18_out, Opcode[0]);
  and and_8 (ALUSrc, not_19_out, not_20_out, not_21_out, Opcode[0]);
  or or_1 (ALUOperation[2], and_3_out, and_1_out, and_4_out);
  or or_2 (ALUOperation[1], and_5_out, and_1_out);
  or or_3 (RegWrite, and_6_out, and_1_out, and_7_out);

  assign ALUOperation[0] = 1'b0;
endmodule

module Arith_Log (
  input  Opcode3,
  input  Opcode2,
  input  Opcode1,
  input  Opcode0,
  input  Unsigned,
  input  Subop,
  output ALUOp3,
  output ALUOp2,
  output ALUOp1,
  output ALUOp0,
  output RegWrite,
  output ALUSrc
);

  wire and_2_out, and_3_out, and_5_out, and_6_out, not_1_out, not_2_out, not_3_out, not_4_out, not_5_out,
       not_6_out, not_7_out, not_8_out, not_9_out, not_10_out, not_11_out, not_12_out, not_13_out,
       not_14_out, not_15_out, not_16_out, not_17_out, not_18_out, not_19_out, not_20_out, not_21_out;

  not not_1 (not_1_out, Opcode3);
  not not_2 (not_2_out, Opcode2);
  not not_3 (not_3_out, Subop);
  not not_4 (not_4_out, Opcode3);
  not not_5 (not_5_out, Opcode2);
  not not_6 (not_6_out, Opcode1);
  not not_7 (not_7_out, Opcode0);
  not not_8 (not_8_out, Opcode3);
  not not_9 (not_9_out, Opcode2);
  not not_10 (not_10_out, Subop);
  not not_11 (not_11_out, Opcode3);
  not not_12 (not_12_out, Opcode2);
  not not_13 (not_13_out, Opcode1);
  not not_14 (not_14_out, Opcode3);
  not not_15 (not_15_out, Opcode2);
  not not_16 (not_16_out, Opcode1);
  not not_17 (not_17_out, Opcode3);
  not not_18 (not_18_out, Opcode2);
  not not_19 (not_19_out, Opcode3);
  not not_20 (not_20_out, Opcode2);
  not not_21 (not_21_out, Opcode1);
  and and_1 (ALUOp3, not_1_out, not_2_out, Opcode1, Opcode0, not_3_out);
  and and_2 (and_2_out, not_4_out, not_5_out, not_6_out, not_7_out, Subop);
  and and_3 (and_3_out, not_8_out, not_9_out, Opcode1, Opcode0, not_10_out);
  and and_4 (ALUOp1, not_11_out, not_12_out, not_13_out);
  and and_5 (and_5_out, not_14_out, not_15_out, not_16_out);
  and and_6 (and_6_out, not_17_out, not_18_out, Opcode0);
  and and_7 (ALUSrc, not_19_out, not_20_out, not_21_out, Opcode0);
  or or_1 (ALUOp2, and_2_out, and_3_out);
  or or_2 (RegWrite, and_5_out, and_6_out);

  assign ALUOp0 = 1'b0;
endmodule

module one_bit_ALU (
  input  Ainvert,
  input  Binvert,
  input  CarryIn,
  input  [1:0] Operation,
  input  a,
  input  b,
  input  Less,
  output Result,
  output Set,
  output CarryOut
);

  wire and_1_out, multiplexer_1_out, multiplexer_2_out, not_1_out, not_2_out, or_1_out;

  not not_1 (not_1_out, a);
  Multiplexer #(.enable("false")) multiplexer_1 (.in0(a), .in1(not_1_out), .out(multiplexer_1_out), .sel(Ainvert));
  not not_2 (not_2_out, b);
  Multiplexer #(.enable("false")) multiplexer_2 (.in0(b), .in1(not_2_out), .out(multiplexer_2_out), .sel(Binvert));
  and and_1 (and_1_out, multiplexer_1_out, multiplexer_2_out);
  or or_1 (or_1_out, multiplexer_1_out, multiplexer_2_out);
  Adder #(.width(1)) adder_1 (.a(multiplexer_1_out), .b(multiplexer_2_out), .out(Set), .cin(CarryIn), .cout(CarryOut));
  Multiplexer #(.select(2), .enable("false")) multiplexer_3 (
    .in0(and_1_out), .in1(or_1_out), .in2(Set), .in3(Less), .out(Result), .sel(Operation));
endmodule

module sixteen_bit_ALU (
  input  [3:0] ALUOperation,
  input  [15:0] a,
  input  [15:0] b,
  output Zero,
  output [15:0] Result,
  output Overflow
);

  wire and_1_out, not_1_out, not_2_out, one_bit_alu_1_carryout, one_bit_alu_2_carryout,
       one_bit_alu_3_carryout, one_bit_alu_4_carryout, one_bit_alu_5_carryout, one_bit_alu_6_carryout,
       one_bit_alu_7_carryout, one_bit_alu_8_carryout, one_bit_alu_9_carryout, one_bit_alu_10_carryout,
       one_bit_alu_11_carryout, one_bit_alu_12_carryout, one_bit_alu_13_carryout, one_bit_alu_14_carryout,
       one_bit_alu_15_carryout, one_bit_alu_16_carryout, one_bit_alu_16_set, xor_1_out;
  wire [15:0] one_bit_alu_1_result, subtractor_1_out;

  Subtractor #(.width(16)) subtractor_1 (.a(a), .b(b), .out(subtractor_1_out));  // open: bin, bout
  one_bit_ALU one_bit_alu_1 (
    .a(a[0]), .b(b[0]), .Less(xor_1_out), .Ainvert(ALUOperation[3]), .Binvert(ALUOperation[2]),
    .CarryIn(ALUOperation[2]), .Operation(ALUOperation[1:0]), .CarryOut(one_bit_alu_1_carryout),
    .Result(one_bit_alu_1_result[0]));  // open: Set
  one_bit_ALU one_bit_alu_2 (
    .a(a[1]), .b(b[1]), .Less(1'b0), .Ainvert(ALUOperation[3]), .Binvert(ALUOperation[2]),
    .CarryIn(one_bit_alu_1_carryout), .Operation(ALUOperation[1:0]), .CarryOut(one_bit_alu_2_carryout),
    .Result(one_bit_alu_1_result[1]));  // open: Set
  one_bit_ALU one_bit_alu_3 (
    .a(a[2]), .b(b[2]), .Less(1'b0), .Ainvert(ALUOperation[3]), .Binvert(ALUOperation[2]),
    .CarryIn(one_bit_alu_2_carryout), .Operation(ALUOperation[1:0]), .CarryOut(one_bit_alu_3_carryout),
    .Result(one_bit_alu_1_result[2]));  // open: Set
  one_bit_ALU one_bit_alu_4 (
    .a(a[3]), .b(b[3]), .Less(1'b0), .Ainvert(ALUOperation[3]), .Binvert(ALUOperation[2]),
    .CarryIn(one_bit_alu_3_carryout), .Operation(ALUOperation[1:0]), .CarryOut(one_bit_alu_4_carryout),
    .Result(one_bit_alu_1_result[3]));  // open: Set
  one_bit_ALU one_bit_alu_5 (
    .a(a[4]), .b(b[4]), .Less(1'b0), .Ainvert(ALUOperation[3]), .Binvert(ALUOperation[2]),
    .CarryIn(one_bit_alu_4_carryout), .Operation(ALUOperation[1:0]), .CarryOut(one_bit_alu_5_carryout),
    .Result(one_bit_alu_1_result[4]));  // open: Set
  one_bit_ALU one_bit_alu_6 (
    .a(a[5]), .b(b[5]), .Less(1'b0), .Ainvert(ALUOperation[3]), .Binvert(ALUOperation[2]),
    .CarryIn(one_bit_alu_5_carryout), .Operation(ALUOperation[1:0]), .CarryOut(one_bit_alu_6_carryout),
    .Result(one_bit_alu_1_result[5]));  // open: Set
  one_bit_ALU one_bit_alu_7 (
    .a(a[6]), .b(b[6]), .Less(1'b0), .Ainvert(ALUOperation[3]), .Binvert(ALUOperation[2]),
    .CarryIn(one_bit_alu_6_carryout), .Operation(ALUOperation[1:0]), .CarryOut(one_bit_alu_7_carryout),
    .Result(one_bit_alu_1_result[6]));  // open: Set
  one_bit_ALU one_bit_alu_8 (
    .a(a[7]), .b(b[7]), .Less(1'b0), .Ainvert(ALUOperation[3]), .Binvert(ALUOperation[2]),
    .CarryIn(one_bit_alu_7_carryout), .Operation(ALUOperation[1:0]), .CarryOut(one_bit_alu_8_carryout),
    .Result(one_bit_alu_1_result[7]));  // open: Set
  one_bit_ALU one_bit_alu_9 (
    .a(a[8]), .b(b[8]), .Less(1'b0), .Ainvert(ALUOperation[3]), .Binvert(ALUOperation[2]),
    .CarryIn(one_bit_alu_8_carryout), .Operation(ALUOperation[1:0]), .CarryOut(one_bit_alu_9_carryout),
    .Result(one_bit_alu_1_result[8]));  // open: Set
  one_bit_ALU one_bit_alu_10 (
    .a(a[9]), .b(b[9]), .Less(1'b0), .Ainvert(ALUOperation[3]), .Binvert(ALUOperation[2]),
    .CarryIn(one_bit_alu_9_carryout), .Operation(ALUOperation[1:0]), .CarryOut(one_bit_alu_10_carryout),
    .Result(one_bit_alu_1_result[9]));  // open: Set
  one_bit_ALU one_bit_alu_11 (
    .a(a[10]), .b(b[10]), .Less(1'b0), .Ainvert(ALUOperation[3]), .Binvert(ALUOperation[2]),
    .CarryIn(one_bit_alu_10_carryout), .Operation(ALUOperation[1:0]), .CarryOut(one_bit_alu_11_carryout),
    .Result(one_bit_alu_1_result[10]));  // open: Set
  one_bit_ALU one_bit_alu_12 (
    .a(a[11]), .b(b[11]), .Less(1'b0), .Ainvert(ALUOperation[3]), .Binvert(ALUOperation[2]),
    .CarryIn(one_bit_alu_11_carryout), .Operation(ALUOperation[1:0]), .CarryOut(one_bit_alu_12_carryout),
    .Result(one_bit_alu_1_result[11]));  // open: Set
  one_bit_ALU one_bit_alu_13 (
    .a(a[12]), .b(b[12]), .Less(1'b0), .Ainvert(ALUOperation[3]), .Binvert(ALUOperation[2]),
    .CarryIn(one_bit_alu_12_carryout), .Operation(ALUOperation[1:0]), .CarryOut(one_bit_alu_13_carryout),
    .Result(one_bit_alu_1_result[12]));  // open: Set
  one_bit_ALU one_bit_alu_14 (
    .a(a[13]), .b(b[13]), .Less(1'b0), .Ainvert(ALUOperation[3]), .Binvert(ALUOperation[2]),
    .CarryIn(one_bit_alu_13_carryout), .Operation(ALUOperation[1:0]), .CarryOut(one_bit_alu_14_carryout),
    .Result(one_bit_alu_1_result[13]));  // open: Set
  one_bit_ALU one_bit_alu_15 (
    .a(a[14]), .b(b[14]), .Less(1'b0), .Ainvert(ALUOperation[3]), .Binvert(ALUOperation[2]),
    .CarryIn(one_bit_alu_14_carryout), .Operation(ALUOperation[1:0]), .CarryOut(one_bit_alu_15_carryout),
    .Result(one_bit_alu_1_result[14]));  // open: Set
  one_bit_ALU one_bit_alu_16 (
    .a(a[15]), .b(b[15]), .Less(1'b0), .Ainvert(ALUOperation[3]), .Binvert(ALUOperation[2]),
    .CarryIn(one_bit_alu_15_carryout), .Operation(ALUOperation[1:0]), .CarryOut(one_bit_alu_16_carryout),
    .Result(one_bit_alu_1_result[15]), .Set(one_bit_alu_16_set));
  xor xor_1 (xor_1_out, one_bit_alu_16_set, Overflow);
  xor xor_2 (Overflow, one_bit_alu_15_carryout, one_bit_alu_16_carryout);
  not not_1 (not_1_out, ALUOperation[0]);
  not not_2 (not_2_out, ALUOperation[3]);
  and and_1 (and_1_out, not_1_out, ALUOperation[1], ALUOperation[2], not_2_out);
  nor nor_1 (Zero, one_bit_alu_1_result[0], one_bit_alu_1_result[1], one_bit_alu_1_result[2], one_bit_alu_1_result[3], one_bit_alu_1_result[4], one_bit_alu_1_result[5], one_bit_alu_1_result[6], one_bit_alu_1_result[7], one_bit_alu_1_result[8], one_bit_alu_1_result[9], one_bit_alu_1_result[10], one_bit_alu_1_result[11], one_bit_alu_1_result[12], one_bit_alu_1_result[13], one_bit_alu_1_result[14], one_bit_alu_1_result[15]);
  Multiplexer #(.width(16), .enable("false")) multiplexer_1 (
    .in0(one_bit_alu_1_result), .in1(subtractor_1_out), .out(Result), .sel(and_1_out));
endmodule

module PCDecoder (
  input  [3:0] Opcode,
  input  Subop,
  input  Zero,
  input  Less,
  output RegtoPC,
  output IMMtoPC,
  output ZerosToALU,
  output [3:0] ALUOp
);

  wire and_4_out, and_5_out, and_6_out, and_7_out, and_8_out, not_1_out, not_2_out, not_3_out, not_4_out,
       not_5_out, not_6_out, not_7_out, not_8_out, not_9_out, not_10_out, not_11_out, not_12_out, not_13_out,
       not_14_out, not_15_out, not_16_out;

  not not_1 (not_1_out, Opcode[2]);
  not not_2 (not_2_out, Opcode[1]);
  not not_3 (not_3_out, Subop);
  not not_4 (not_4_out, Opcode[2]);
  not not_5 (not_5_out, Opcode[1]);
  not not_6 (not_6_out, Opcode[0]);
  not not_7 (not_7_out, Opcode[2]);
  not not_8 (not_8_out, Opcode[1]);
  not not_9 (not_9_out, Zero);
  not not_10 (not_10_out, Opcode[2]);
  not not_11 (not_11_out, Zero);
  not not_12 (not_12_out, Opcode[0]);
  not not_13 (not_13_out, Zero);
  not not_14 (not_14_out, Less);
  not not_15 (not_15_out, Opcode[0]);
  and and_1 (ZerosToALU, Opcode[3], not_16_out);
  not not_16 (not_16_out, Opcode[2]);
  and and_2 (ALUOp[1], Opcode[3], not_1_out);
  and and_3 (RegtoPC, Opcode[3], Opcode[2], not_2_out, Opcode[0], not_3_out);
  and and_4 (and_4_out, Opcode[3], not_4_out, not_5_out, not_6_out, Zero);
  and and_5 (and_5_out, Opcode[3], not_7_out, not_8_out, Opcode[0], not_9_out);
  and and_6 (and_6_out, Opcode[3], not_10_out, Opcode[0], not_11_out, Less);
  and and_7 (and_7_out, Opcode[3], Opcode[1], not_12_out, not_13_out, not_14_out);
  and and_8 (and_8_out, Opcode[3], Opcode[2], Opcode[1], not_15_out);
  or or_1 (IMMtoPC, and_4_out, and_5_out, and_6_out, and_7_out, and_8_out);

  assign {ALUOp[3:2], ALUOp[0]} = 3'b000;
endmodule

module PCDecoderLogic (
  input  Opcode3,
  input  Opcode2,
  input  Opcode1,
  input  Opcode0,
  input  Subop,
  input  Zero,
  input  Less,
  output RegtoPC,
  output IMMtoPC,
  output OnestoALU
);

  wire and_2_out, and_3_out, and_4_out, and_5_out, and_6_out, not_1_out, not_2_out, not_3_out, not_4_out,
       not_5_out, not_6_out, not_7_out, not_8_out, not_9_out, not_10_out, not_11_out, not_12_out, not_13_out,
       not_14_out, not_15_out;

  not not_1 (not_1_out, Opcode1);
  not not_2 (not_2_out, Subop);
  not not_3 (not_3_out, Opcode2);
  not not_4 (not_4_out, Opcode1);
  not not_5 (not_5_out, Opcode0);
  not not_6 (not_6_out, Opcode2);
  not not_7 (not_7_out, Opcode1);
  not not_8 (not_8_out, Zero);
  not not_9 (not_9_out, Opcode2);
  not not_10 (not_10_out, Zero);
  not not_11 (not_11_out, Opcode0);
  not not_12 (not_12_out, Zero);
  not not_13 (not_13_out, Less);
  not not_14 (not_14_out, Opcode0);
  not not_15 (not_15_out, Opcode2);
  and and_1 (RegtoPC, Opcode3, Opcode2, not_1_out, Opcode0, not_2_out);
  and and_2 (and_2_out, Opcode3, not_3_out, not_4_out, not_5_out, Zero);
  and and_3 (and_3_out, Opcode3, not_6_out, not_7_out, Opcode0, not_8_out);
  and and_4 (and_4_out, Opcode3, not_9_out, Opcode0, not_10_out, Less);
  and and_5 (and_5_out, Opcode3, Opcode1, not_11_out, not_12_out, not_13_out);
  and and_6 (and_6_out, Opcode3, Opcode2, Opcode1, not_14_out);
  and and_7 (OnestoALU, Opcode3, not_15_out);
  or or_1 (IMMtoPC, and_2_out, and_3_out, and_4_out, and_5_out, and_6_out);
endmodule

module Decoder (
  input  [3:0] Opcode,
  input  Subop,
  input  Zero,
  input  Less,
  output ShiftSrc,
  output ShifterToReg,
  output RegWrite,
  output [3:0] ALUOp,
  output IMMtoALU,
  output RegtoPC,
  output IMMtoPC,
  output ZerosToALU,
  output MemWrite,
  output MemtoReg,
  output Halt,
  output LED,
  output WriteLED,
  output MemRead,
  output PCtoReg
);

  wire Arith_LogDecoder_regwrite, JALDecoder_immtopc, JALDecoder_regwrite, MemDecoder_regwrite,
       PCDecoder_immtopc, ShifterDecoder_regwrite;
  wire [3:0] Arith_LogDecoder_aluoperation, PCDecoder_aluop;

  ShifterDecoder ShifterDecoder (
    .Opcode(Opcode), .ShiftSrc(ShiftSrc), .ShiftertoReg(ShifterToReg), .RegWrite(ShifterDecoder_regwrite));
  Arith_Log_Decoder Arith_LogDecoder (
    .Opcode(Opcode), .Subop(Subop), .ALUOperation(Arith_LogDecoder_aluoperation),
    .RegWrite(Arith_LogDecoder_regwrite), .ALUSrc(IMMtoALU));
  PCDecoder PCDecoder (
    .Opcode(Opcode), .Subop(Subop), .Zero(Zero), .Less(Less), .RegtoPC(RegtoPC), .IMMtoPC(PCDecoder_immtopc),
    .ZerosToALU(ZerosToALU), .ALUOp(PCDecoder_aluop));
  MemDecoder MemDecoder (
    .Opcode(Opcode), .Subop(Subop), .MemWrite(MemWrite), .MemtoReg(MemtoReg), .RegWrite(MemDecoder_regwrite),
    .MemRead(MemRead));
  HaltDecoder haltdecoder_1 (.Opcode(Opcode), .Halt(Halt), .LED(LED));
  PutDecoder PutDecoder (.Opcode(Opcode), .WriteLED(WriteLED));
  JALDecoder JALDecoder (
    .Opcode(Opcode), .IMMtoPC(JALDecoder_immtopc), .PCtoReg(PCtoReg), .RegWrite(JALDecoder_regwrite));
  or or_1 (RegWrite, ShifterDecoder_regwrite, Arith_LogDecoder_regwrite, MemDecoder_regwrite, JALDecoder_regwrite);
  or or_2 (IMMtoPC, PCDecoder_immtopc, JALDecoder_immtopc);
  assign ALUOp = Arith_LogDecoder_aluoperation | PCDecoder_aluop;  // OR_Gate or_3, 4 bits wide
endmodule

module MemDecoder (
  input  [3:0] Opcode,
  input  Subop,
  output MemWrite,
  output MemtoReg,
  output RegWrite,
  output MemRead
);

  and and_1 (MemWrite, ~Opcode[0], Opcode[1], Opcode[2], ~Opcode[3], Subop);  // AND_Gate
  and and_2 (MemRead, ~Opcode[0], Opcode[1], Opcode[2], ~Opcode[3], ~Subop);  // AND_Gate

  assign MemtoReg = MemRead;
  assign RegWrite = MemRead;
endmodule

module HaltDecoder (
  input  [3:0] Opcode,
  output Halt,
  output LED
);

  and and_1 (Halt, ~Opcode[3], Opcode[2], Opcode[1], Opcode[0]);  // AND_Gate

  assign LED = Halt;
endmodule

module PutDecoder (
  input  [3:0] Opcode,
  output WriteLED
);

  and and_1 (WriteLED, Opcode[0], Opcode[1], Opcode[2], Opcode[3]);
endmodule

module JALDecoder (
  input  [3:0] Opcode,
  output IMMtoPC,
  output PCtoReg,
  output RegWrite
);

  and and_1 (IMMtoPC, ~Opcode[0], ~Opcode[1], Opcode[2], Opcode[3]);  // AND_Gate

  assign PCtoReg = IMMtoPC;
  assign RegWrite = IMMtoPC;
endmodule

module ResultToLess (
  input  [15:0] Result,
  output Less
);


  assign Less = Result[15];
endmodule

module side (
  input  Op3,
  input  Op2,
  input  Op1,
  input  Op0,
  output Op3_2,
  output Op2_2,
  output Op1_2,
  output Op0_2
);

  wire not_1_out;

  and and_1 (Op1_2, Op3, not_1_out);
  not not_1 (not_1_out, Op2);

  assign Op0_2 = 1'b0;
  assign Op2_2 = 1'b0;
  assign Op3_2 = 1'b0;
endmodule

module IF_ID (
  input  [15:0] ROM_in,
  input  Halt_in,
  input  clk,
  output [15:0] ROM_out,
  output Halt_out
);

  Register #(.width(16)) register_1 (.D(ROM_in), .Q(ROM_out), .clk(clk));  // open: en, clr
  Register #(.width(1)) register_2 (.D(Halt_in), .Q(Halt_out), .clk(clk));  // open: en, clr
endmodule

module ID_EX (
  input  [15:0] ReadData1,
  input  [15:0] The_signal_that_goes_into_the_mux_that_goes_into_the_ALU,
  input  [15:0] ReadData2,
  input  SubOp,
  input  ShiftSrc,
  input  [3:0] ShiftAmount,
  input  [7:0] PC_1,
  input  ZerosToALU,
  input  MemWrite,
  input  MemToReg,
  input  LED,
  input  WriteLED,
  input  MemRead,
  input  PCtoReg,
  input  ShifterToReg,
  input  [3:0] ALUOp,
  input  RegWrite,
  input  [2:0] WriteRegister,
  input  [2:0] rtReg,
  input  IMMtoALU,
  input  clk,
  output [15:0] ReadData1_2,
  output [15:0] The_signal_that_goes_into_the_mux_that_goes_into_the_ALU_2,
  output [15:0] ReadData2_2,
  output SubOp_2,
  output ShiftSrc_2,
  output [3:0] ShiftAmount_2,
  output [7:0] PC_1_2,
  output ZerosToALU_2,
  output MemWrite_2,
  output MemToReg_2,
  output LED_2,
  output WriteLED_2,
  output MemRead_2,
  output PCtoReg_2,
  output ShifterToReg_2,
  output [3:0] ALUOp_2,
  output RegWrite_2,
  output [2:0] WriteRegister_2,
  output [2:0] rtReg_2,
  output IMMtoALU_2
);

  Register #(.width(16)) register_1 (.D(ReadData1), .Q(ReadData1_2), .clk(clk));  // open: en, clr
  Register #(.width(16)) register_2 (
    .D(The_signal_that_goes_into_the_mux_that_goes_into_the_ALU),
    .Q(The_signal_that_goes_into_the_mux_that_goes_into_the_ALU_2), .clk(clk));  // open: en, clr
  Register #(.width(16)) register_3 (.D(ReadData2), .Q(ReadData2_2), .clk(clk));  // open: en, clr
  Register #(.width(1)) register_4 (.D(SubOp), .Q(SubOp_2), .clk(clk));  // open: en, clr
  Register #(.width(1)) register_5 (.D(ShiftSrc), .Q(ShiftSrc_2), .clk(clk));  // open: en, clr
  Register #(.width(4)) register_6 (.D(ShiftAmount), .Q(ShiftAmount_2), .clk(clk));  // open: en, clr
  Register register_7 (.D(PC_1), .Q(PC_1_2), .clk(clk));  // open: en, clr
  Register #(.width(1)) register_8 (.D(ZerosToALU), .Q(ZerosToALU_2), .clk(clk));  // open: en, clr
  Register #(.width(1)) register_9 (.D(MemWrite), .Q(MemWrite_2), .clk(clk));  // open: en, clr
  Register #(.width(1)) register_10 (.D(MemToReg), .Q(MemToReg_2), .clk(clk));  // open: en, clr
  Register #(.width(1)) register_11 (.D(LED), .Q(LED_2), .clk(clk));  // open: en, clr
  Register #(.width(1)) register_12 (.D(WriteLED), .Q(WriteLED_2), .clk(clk));  // open: en, clr
  Register #(.width(1)) register_13 (.D(MemRead), .Q(MemRead_2), .clk(clk));  // open: en, clr
  Register #(.width(1)) register_14 (.D(PCtoReg), .Q(PCtoReg_2), .clk(clk));  // open: en, clr
  Register #(.width(1)) register_15 (.D(ShifterToReg), .Q(ShifterToReg_2), .clk(clk));  // open: en, clr
  Register #(.width(4)) register_16 (.D(ALUOp), .Q(ALUOp_2), .clk(clk));  // open: en, clr
  Register #(.width(1)) register_17 (.D(RegWrite), .Q(RegWrite_2), .clk(clk));  // open: en, clr
  Register #(.width(3)) register_18 (.D(WriteRegister), .Q(WriteRegister_2), .clk(clk));  // open: en, clr
  Register #(.width(3)) register_19 (.D(rtReg), .Q(rtReg_2), .clk(clk));  // open: en, clr
  Register #(.width(1)) register_20 (.D(IMMtoALU), .Q(IMMtoALU_2), .clk(clk));  // open: en, clr
endmodule

module EX_MEM (
  input  [15:0] ReadData1,
  input  [15:0] ALU_Result,
  input  [15:0] ReadData2,
  input  SubOp,
  input  ShiftSrc,
  input  [3:0] ShiftAmount,
  input  [7:0] PC_1,
  input  ShifterToReg,
  input  MemWrite,
  input  MemToReg,
  input  LED,
  input  WriteLED,
  input  MemRead,
  input  PCtoReg,
  input  RegWrite,
  input  [2:0] WriteRegister,
  input  clk,
  output [15:0] ReadData1_2,
  output [15:0] ALU_Result_2,
  output [15:0] ReadData2_2,
  output SubOp_2,
  output ShiftSrc_2,
  output [3:0] ShiftAmount_2,
  output [7:0] PC_1_2,
  output ShifterToReg_2,
  output MemWrite_2,
  output MemToReg_2,
  output LED_2,
  output WriteLED_2,
  output MemRead_2,
  output PCtoReg_2,
  output RegWrite_2,
  output [2:0] WriteRegister_2
);

  Register #(.width(16)) register_1 (.D(ReadData1), .Q(ReadData1_2), .clk(clk));  // open: en, clr
  Register #(.width(16)) register_2 (.D(ALU_Result), .Q(ALU_Result_2), .clk(clk));  // open: en, clr
  Register #(.width(16)) register_3 (.D(ReadData2), .Q(ReadData2_2), .clk(clk));  // open: en, clr
  Register #(.width(1)) register_4 (.D(SubOp), .Q(SubOp_2), .clk(clk));  // open: en, clr
  Register #(.width(1)) register_5 (.D(ShiftSrc), .Q(ShiftSrc_2), .clk(clk));  // open: en, clr
  Register #(.width(4)) register_6 (.D(ShiftAmount), .Q(ShiftAmount_2), .clk(clk));  // open: en, clr
  Register register_7 (.D(PC_1), .Q(PC_1_2), .clk(clk));  // open: en, clr
  Register #(.width(1)) register_8 (.D(ShifterToReg), .Q(ShifterToReg_2), .clk(clk));  // open: en, clr
  Register #(.width(1)) register_9 (.D(MemWrite), .Q(MemWrite_2), .clk(clk));  // open: en, clr
  Register #(.width(1)) register_10 (.D(MemToReg), .Q(MemToReg_2), .clk(clk));  // open: en, clr
  Register #(.width(1)) register_11 (.D(LED), .Q(LED_2), .clk(clk));  // open: en, clr
  Register #(.width(1)) register_12 (.D(WriteLED), .Q(WriteLED_2), .clk(clk));  // open: en, clr
  Register #(.width(1)) register_13 (.D(MemRead), .Q(MemRead_2), .clk(clk));  // open: en, clr
  Register #(.width(1)) register_14 (.D(PCtoReg), .Q(PCtoReg_2), .clk(clk));  // open: en, clr
  Register #(.width(1)) register_15 (.D(RegWrite), .Q(RegWrite_2), .clk(clk));  // open: en, clr
  Register #(.width(3)) register_16 (.D(WriteRegister), .Q(WriteRegister_2), .clk(clk));  // open: en, clr
endmodule

module MEM_WB (
  input  [15:0] RAM_Data,
  input  [15:0] ALU_Result,
  input  SubOp,
  input  [15:0] ReadData1,
  input  [15:0] ReadData2,
  input  ShiftSrc,
  input  [3:0] ShiftAmount,
  input  [7:0] PC_1,
  input  ShifterToReg,
  input  PCtoReg,
  input  MemToReg,
  input  LED,
  input  WriteLED,
  input  RegWrite,
  input  [2:0] WriteRegister,
  input  clk,
  output [15:0] RAM_Data_2,
  output [15:0] ALU_Result_2,
  output SubOp_2,
  output [15:0] ReadData1_2,
  output [15:0] ReadData2_2,
  output ShiftSrc_2,
  output [3:0] ShiftAmount_2,
  output [7:0] PC_1_2,
  output ShifterToReg_2,
  output PCtoReg_2,
  output MemToReg_2,
  output LED_2,
  output WriteLED_2,
  output RegWrite_2,
  output [2:0] WriteRegister_2
);

  Register #(.width(16)) register_1 (.D(RAM_Data), .Q(RAM_Data_2), .clk(clk));  // open: en, clr
  Register #(.width(16)) register_2 (.D(ALU_Result), .Q(ALU_Result_2), .clk(clk));  // open: en, clr
  Register #(.width(1)) register_3 (.D(SubOp), .Q(SubOp_2), .clk(clk));  // open: en, clr
  Register #(.width(16)) register_4 (.D(ReadData1), .Q(ReadData1_2), .clk(clk));  // open: en, clr
  Register #(.width(16)) register_5 (.D(ReadData2), .Q(ReadData2_2), .clk(clk));  // open: en, clr
  Register #(.width(1)) register_6 (.D(ShiftSrc), .Q(ShiftSrc_2), .clk(clk));  // open: en, clr
  Register #(.width(4)) register_7 (.D(ShiftAmount), .Q(ShiftAmount_2), .clk(clk));  // open: en, clr
  Register register_8 (.D(PC_1), .Q(PC_1_2), .clk(clk));  // open: en, clr
  Register #(.width(1)) register_9 (.D(ShifterToReg), .Q(ShifterToReg_2), .clk(clk));  // open: en, clr
  Register #(.width(1)) register_10 (.D(PCtoReg), .Q(PCtoReg_2), .clk(clk));  // open: en, clr
  Register #(.width(1)) register_11 (.D(MemToReg), .Q(MemToReg_2), .clk(clk));  // open: en, clr
  Register #(.width(1)) register_12 (.D(LED), .Q(LED_2), .clk(clk));  // open: en, clr
  Register #(.width(1)) register_13 (.D(WriteLED), .Q(WriteLED_2), .clk(clk));  // open: en, clr
  Register #(.width(1)) register_14 (.D(RegWrite), .Q(RegWrite_2), .clk(clk));  // open: en, clr
  Register #(.width(3)) register_15 (.D(WriteRegister), .Q(WriteRegister_2), .clk(clk));  // open: en, clr
endmodule

module Forwarding_Unit (
  input  [2:0] rs_ID_EX,
  input  [2:0] rt_ID_EX,
  input  [2:0] WriteReg_MEM_WB,
  input  [2:0] WriteReg_EM_MEM,
  input  RegWrite_EX_MEM,
  input  RegWrite_MEM_WB,
  output A_EX_MEM,
  output A_MEM_WB,
  output B_EX_MEM,
  output B_MEM_WB
);

  wire comparator_1_eq, comparator_2_eq, comparator_3_eq, comparator_4_eq;

  Comparator #(.width(3)) comparator_1 (.a(WriteReg_MEM_WB), .b(rs_ID_EX), .eq(comparator_1_eq));  // open: gt, lt
  Comparator #(.width(3)) comparator_2 (.a(WriteReg_EM_MEM), .b(rs_ID_EX), .eq(comparator_2_eq));  // open: gt, lt
  Comparator #(.width(3)) comparator_3 (.a(WriteReg_MEM_WB), .b(rt_ID_EX), .eq(comparator_3_eq));  // open: gt, lt
  Comparator #(.width(3)) comparator_4 (.a(WriteReg_EM_MEM), .b(rt_ID_EX), .eq(comparator_4_eq));  // open: gt, lt
  and and_1 (A_EX_MEM, comparator_1_eq, RegWrite_EX_MEM);
  and and_2 (A_MEM_WB, comparator_2_eq, RegWrite_MEM_WB);
  and and_3 (B_EX_MEM, comparator_3_eq, RegWrite_EX_MEM);
  and and_4 (B_MEM_WB, comparator_4_eq, RegWrite_MEM_WB);
endmodule
